# Fritzing sketch Line-follower-circuit-diagram (saved by Fritzing 0.9.3b)

parts:
  Part1 = Arduino Mega 2560 (Rev3)
  S1 = Pololu QTR-8 Reflectabce Sensor array [package=THT]
  L298N1 = L298N DC motor driver
  M1 = Getriebemotor
  M2 = Getriebemotor
  VCC1 = 4 x AAA Battery Mount
  S2 = Taiway 100-SP-X-T1 SPDT Miniature Toggle Switch [part_number=100-SP-X-T1-0-0-B1-M1 package=THT]
  BAT1 = BC9VPC [package=bc9vpc]
  S3 = Taiway 100-SP-X-T1 SPDT Miniature Toggle Switch [part_number=100-SP-X-T1-0-0-B1-M1 package=THT]

nets:
  N1: Part1.A0, S1.pin12
  N2: Part1.A1, S1.pin11
  N3: Part1.A2, S1.pin10
  N4: Part1.A3, S1.pin9
  N5: Part1.A4, S1.pin8
  N6: Part1.A5, S1.pin7
  N7: Part1.A6, S1.pin4, S1.pin6
  N8: Part1.A7, S1.pin3, S1.pin5
  N9: Part1.5V, S1.pin2, S1.pin14
  N10: Part1.GND, S1.pin1, S1.pin15, BAT1.V-
  N11: Part1.VIN, S3.L1
  N12: Part1.D2_PWM, L298N1.ENB
  N13: Part1.D3_PWM, L298N1.ENA
  N14: Part1.D22, L298N1.IN1
  N15: Part1.D24, L298N1.IN2
  N16: Part1.D32, L298N1.IN4
  N17: Part1.D34, L298N1.IN3
  N18: L298N1.OUT1, M2.pin_2
  N19: L298N1.OUT2, M2.pin_1
  N20: L298N1.OUT3, M1.pin_2
  N21: L298N1.OUT4, M1.pin_1
  N22: L298N1.12V, S2.L1
  N23: L298N1.GND, VCC1.-
  N24: VCC1.+, S2.L2
  N25: BAT1.V+, S3.L2

custom parts:
  L298N DC motor driver: 2x DC motor driver with 78M05 positive voltage regulator (7..35 V) L298N: max 46 V, 2 A Set 5 V Enable jumper to enable 5 V regultor (needed for the L298N) and +5 V output at screw terminal or supply external +5 V at screw terminal Set ENA and/or ENB to +5 V to enable motor permanently or supply ENA and/or ENB with PWM signal IN1 and IN2 set rotation directory for motor A (OUT1/OUT2) IN2 and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
